// Logisim project 1805106.circ as structural Verilog: 1 circuit, main circuit main
module main (
  input  P,
  input  Q,
  input  R,
  input  S,
  output F
);

  // _7432 7432_1: pin names not known; wires that end beside it: Q, S, F, 1'b0, 1'b1

  // Notes on the sheet:
  //   f(P,Q,R,S) = Q+S
endmodule
