// Logisim project 1805106.circ as structural Verilog: 1 circuit, main circuit main
module main (
  input  A,
  input  B,
  input  C,
  input  D,
  output F
);

  wire n74157_1_p4;

  // _74157 74157_1: pin names not known; wires that end beside it: D, 1'b1, 1'b0, n74157_1_p4, 1'b0, 1'b1, 1'b0
  // _74151 74151_1: pin names not known; wires that end beside it: n74157_1_p4, 1'b0, n74157_1_p4, 1'b1, F, 1'b0, 1'b0, 1'b1, 1'b0, D, 1'b0, D, C, B, A
endmodule
