// Logisim project 1805106.circ as structural Verilog: 1 circuit, main circuit main
module main (
  input  CLR,
  output Y1,
  output Y0
);

  wire CP_out, n7476_1_p3;

  Clock CP (.out(CP_out));
  // _7476 7476_1: pin names not known; wires that end beside it: CP_out, CLR, n7476_1_p3, 1'b1, CP_out, CLR, n7476_1_p3, Y1, 1'b0, 1'b1, Y0, n7476_1_p3, 1'b1
endmodule
