// Logisim project 1805106.circ as structural Verilog: 1 circuit, main circuit main
module main (
  input  X1,
  input  X0,
  output Y1,
  output Y0,
  output Z1,
  output Z2
);

  wire CP_out, n7404_1_p2, n7404_1_p6, n7408_2_p3, n7408_2_p6, n7408_2_p10, n7408_2_p11, n7408_2_p14,
       n7432_1_p3, n7432_1_p6, n7432_1_p11, n7432_1_p12, n7432_1_p13, n7432_1_p14, n7474_1_p1, n7474_1_p6,
       n7476_1_p2, n7476_1_p10;

  Clock CP (.out(CP_out));
  // _7404 7404_1: pin names not known; wires that end beside it: X1, n7404_1_p2, 1'b0, 1'b1, X0, n7404_1_p6
  // _7432 7432_1: pin names not known; wires that end beside it: X0, Y0, n7432_1_p3, X0, Y1, n7432_1_p6, 1'b0, 1'b1, Y0, X1, n7432_1_p11, n7432_1_p12, n7432_1_p13, n7432_1_p14
  // _7476 7476_1: pin names not known; wires that end beside it: CP_out, n7476_1_p2, 1'b1, CP_out, n7432_1_p14, Y1, 1'b0, n7404_1_p2, Y0, n7476_1_p10
  // _7408 7408_1: pin names not known; wires that end beside it: n7432_1_p11, n7404_1_p6, n7476_1_p2, n7432_1_p3, n7404_1_p2, n7432_1_p12, 1'b0, 1'b1, n7404_1_p2, n7404_1_p6, n7476_1_p10, n7404_1_p6, X1, n7432_1_p13
  // _7474 7474_1: pin names not known; wires that end beside it: n7474_1_p1, CP_out, Z1, 1'b0, 1'b1, n7474_1_p6, CP_out, Z2
  // _7408 7408_2: pin names not known; wires that end beside it: n7432_1_p6, X1, n7408_2_p3, n7404_1_p6, Y1, n7408_2_p6, 1'b0, 1'b1, X0, n7408_2_p10, n7408_2_p11, Y0, n7408_2_p6, n7408_2_p14
  // _7432 7432_2: pin names not known; wires that end beside it: n7408_2_p3, n7408_2_p14, n7474_1_p1, Y0, Y1, n7408_2_p10, Z1, 1'b1
  // _7408 7408_3: pin names not known; wires that end beside it: n7408_2_p11, n7404_1_p2, n7474_1_p6, 1'b0, 1'b1
endmodule
